# Fritzing sketch Fan_control (saved by Fritzing 0.9.3b)

parts:
  X2 = USB Connectors [package=usb-a-pcb]
  Power_plug1 = Power plug
  M1 = DC Motor
  S1 = H-Bridge with L298N
  Part1 = Arduino Uno (Rev3) - ICSP

nets:
  N1: X2.D-, Part1.D1/TX
  N2: X2.D+, Part1.D0/RX
  VCC: Power_plug1.VCC, S1.12V
  N3: M1.pin_1, S1.OUT4-Motor2
  GND: S1.GND, Part1.GND
  5V: S1.5V, Part1.5V
  N4: S1.IN1, Part1.D6_PWM
  N5: S1.IN2, Part1.D5_PWM

custom parts:
  H-Bridge with L298N: h-bridge
