# Fritzing sketch Veclocity_control (saved by Fritzing 0.9.3b)

parts:
  Power_plug2 = Power plug
  X3 = USB Connectors [package=usb-a-pcb]
  Part3 = Arduino Nano (Rev3.0)
  Part4 = KY-003 Hall Magnetic Sensor Module [package="Breakout board"]
  S2 = Round Pushbutton

nets:
  GND: Power_plug2.GND, Part3.GND, S2.leg1
  VCC: Power_plug2.VCC, Part3.5V
  N1: X3.D-, Part3.D0/RX
  N2: X3.D+, Part3.D1/TX
  N3: Part3.D2, S2.leg0
  N4: Part3.A0, Part4.S

custom parts:
  KY-003 Hall Magnetic Sensor Module: KEYES KY-003 Arduino Hall Magnetic Sensor Module is a switch that will turn on/off in the presence of a magnetic field.
